# Fritzing sketch qmu_beacon_locator_diagram (saved by Fritzing 0.9.3b)
breadboards: 1

parts:
  S1 = Pushbutton [package="[THT]"]
  S2 = Pushbutton [package="[THT]"]

nets:
  ESP32 LoRa32 pin 4: S1.Pin_1
  1S LiPo Battery -/ESP32 LoRa32 Battery -/GND/GPS GND: S1.Pin_3, S2.Pin_3, S2.Pin_4
  ESP32 LoRa32 pin 0: S2.Pin_1, S2.Pin_2
